// Logisim project projeto1.circ as structural Verilog: 6 circuits, main circuit \-- somador de dois bits
module ULA (
  input  [7:0] A,
  input  [7:0] B,
  input  [1:0] S,
  output [7:0] R,
  output o0,
  output o1,
  output o2,
  output o3
);

  wire soma_1_o0, \subtração_1_out_4 ;
  wire [7:0] soma_1_s, \subtração_1_out_3 , undriven;

  \Subtração  \subtração_1  (.in_1(A), .out_3(\subtração_1_out_3 ), .out_4(\subtração_1_out_4 ), .in_2(B));
  Comparador comparador_1 (.A(A), .o3(o3), .o2(o2), .o1(o1));
  Soma soma_1 (.a(B), .S(soma_1_s), .o0(soma_1_o0), .b(A));
  or or_1 (o0, soma_1_o0, \subtração_1_out_4 );
  Multiplexer #(.select(2), .width(8)) multiplexer_1 (
    .in0(soma_1_s), .in1(\subtração_1_out_3 ), .in2(undriven), .in3(undriven), .out(R), .sel(S));  // open: en
endmodule

module Soma (
  input  [7:0] b,
  input  [7:0] a,
  output [7:0] S,
  output o0
);

  wire somador_de_dois_bits_1_cout, somador_de_dois_bits_2_cout, somador_de_dois_bits_3_cout,
       somador_de_dois_bits_4_cout, somador_de_dois_bits_5_cout, somador_de_dois_bits_6_cout,
       somador_de_dois_bits_7_cout, somador_de_dois_bits_8_cout;

  somador_de_dois_bits somador_de_dois_bits_1 (
    .cin(1'b0), .a(a[0]), .b(b[0]), .Cout(somador_de_dois_bits_1_cout), .s(S[0]));
  somador_de_dois_bits somador_de_dois_bits_2 (
    .cin(somador_de_dois_bits_1_cout), .a(a[1]), .b(b[1]), .Cout(somador_de_dois_bits_2_cout), .s(S[1]));
  somador_de_dois_bits somador_de_dois_bits_3 (
    .cin(somador_de_dois_bits_2_cout), .a(a[2]), .b(b[2]), .Cout(somador_de_dois_bits_3_cout), .s(S[2]));
  somador_de_dois_bits somador_de_dois_bits_4 (
    .cin(somador_de_dois_bits_3_cout), .a(a[3]), .b(b[3]), .Cout(somador_de_dois_bits_4_cout), .s(S[3]));
  somador_de_dois_bits somador_de_dois_bits_5 (
    .cin(somador_de_dois_bits_4_cout), .a(a[4]), .b(b[4]), .Cout(somador_de_dois_bits_5_cout), .s(S[4]));
  somador_de_dois_bits somador_de_dois_bits_6 (
    .cin(somador_de_dois_bits_5_cout), .a(a[5]), .b(b[5]), .Cout(somador_de_dois_bits_6_cout), .s(S[5]));
  somador_de_dois_bits somador_de_dois_bits_7 (
    .cin(somador_de_dois_bits_6_cout), .a(a[6]), .b(b[6]), .Cout(somador_de_dois_bits_7_cout), .s(S[6]));
  somador_de_dois_bits somador_de_dois_bits_8 (
    .cin(somador_de_dois_bits_7_cout), .a(a[7]), .b(b[7]), .Cout(somador_de_dois_bits_8_cout), .s(S[7]));
  xor xor_1 (o0, somador_de_dois_bits_7_cout, somador_de_dois_bits_8_cout);
endmodule

module somador_de_dois_bits (
  input  cin,
  input  a,
  input  b,
  output Cout,
  output s
);

  wire and_1_out, and_2_out, xor_1_out;

  xor xor_1 (xor_1_out, a, b);
  and and_1 (and_1_out, a, b);
  and and_2 (and_2_out, cin, xor_1_out);
  xor xor_2 (s, xor_1_out, cin);
  or or_1 (Cout, and_2_out, and_1_out);
endmodule

module \Subtração  (
  input  [7:0] in_1,
  input  [7:0] in_2,
  output [7:0] out_3,
  output out_4
);

  wire [7:0] complemento_de_dois_1_out_2;

  complemento_de_dois complemento_de_dois_1 (.in_1(in_2), .out_2(complemento_de_dois_1_out_2));
  Soma soma_1 (.a(complemento_de_dois_1_out_2), .S(out_3), .o0(out_4), .b(in_1));
endmodule

module complemento_de_dois (
  input  [7:0] in_1,
  output [7:0] out_2
);

  wire [7:0] not_1_out;

  assign not_1_out = ~in_1;  // NOT_Gate not_1, 8 bits wide
  Soma soma_1 (.a(8'h1), .S(out_2), .b(not_1_out));  // open: o0
endmodule

module Comparador (
  input  [7:0] A,
  output o1,
  output o2,
  output o3
);

  wire or_1_out, or_2_out;

  or or_1 (or_1_out, A[7], A[6], A[5], A[4], A[3], A[2], A[1], A[0]);
  not not_1 (o2, or_1_out);
  or or_2 (or_2_out, o2, A[7]);
  not not_2 (o3, or_2_out);

  assign o1 = A[7];
endmodule
