// Logisim project Projeto2.circ as structural Verilog: 2 circuits, main circuit main
module main (
  input  in_1,
  input  in_2,
  input  in_3,
  input  in_4,
  output [15:0] out_5
);

  wire _0b, _0c, _1f, _15, _16, _29, _33, _38, _46, and_1_out, and_2_out, and_3_out, and_4_out, and_5_out,
       and_6_out, clock_1_out, not_1_out, not_2_out, or_1_out;
  wire [7:0] counter_1_q, multiplexer_1_out, p0b, PC_q;
  wire [15:0] ram_1_data;
  wire [15:8] IR_q;

  and and_1 (and_1_out, _0b, 1'b1);
  Clock clock_1 (.out(clock_1_out));
  and and_2 (and_2_out, clock_1_out, or_1_out);
  or or_1 (or_1_out, and_3_out, and_4_out, and_6_out);
  not not_1 (not_1_out, and_1_out);
  Register #(.width(16)) ACC (.D(ram_1_data), .Q(out_5), .clk(and_2_out), .clr(in_4));  // open: en
  Counter counter_1 (
    .load(and_1_out), .D(counter_1_q), .count(not_1_out), .Q(counter_1_q), .clk(clock_1_out), .clr(in_4));  // open: carry
  Counter PC (.load(and_1_out), .D(p0b), .count(1'b0), .Q(PC_q), .clk(clock_1_out), .clr(in_4));  // open: carry
  and and_3 (and_3_out, _0b, 1'b1);
  and and_4 (and_4_out, _15, 1'b1);
  and and_5 (and_5_out, _0b, ~clock_1_out);  // AND_Gate
  and and_6 (and_6_out, _16, 1'b1);
  Multiplexer #(.width(8)) multiplexer_1 (
    .in0(counter_1_q), .in1(PC_q), .out(multiplexer_1_out), .sel(and_5_out), .en(not_2_out));
  not not_2 (not_2_out, and_5_out);
  RAM #(.dataWidth(16), .bus("separate")) ram_1 (
    .addr(multiplexer_1_out), .data(ram_1_data), .str(in_1), .clk(clock_1_out), .ld(in_2), .clr(in_3));  // open: din, sel
  Register #(.width(16)) IR (.D(ram_1_data), .en(clock_1_out), .Q({IR_q, p0b}), .clk(clock_1_out), .clr(in_4));
  // AND_Gate and_7 has open pins: in0=_46, in1=1'b1, out=open
  // AND_Gate and_8 has open pins: in0=_1f, in1=1'b1, out=open
  // AND_Gate and_9 has open pins: in0=_29, in1=1'b1, out=open
  // AND_Gate and_10 has open pins: in0=_38, in1=1'b1, out=open
  Seletor seletor_1 (
    .in_1(IR_q[15]), .in_2(IR_q[14]), .in_3(IR_q[13]), .in_4(IR_q[12]), .in_5(IR_q[11]), .in_6(IR_q[10]),
    .in_7(IR_q[9]), .in_8(IR_q[8]), ._0b(_0b), ._0c(_0c), ._33(_33), ._15(_15), ._38(_38), ._16(_16),
    ._46(_46), ._1f(_1f), ._29(_29));
  // AND_Gate and_11 has open pins: in0=_0c, in1=1'b1, out=open
  // AND_Gate and_12 has open pins: in0=_33, in1=1'b1, out=open
endmodule

module Seletor (
  input  in_1,
  input  in_2,
  input  in_3,
  input  in_4,
  input  in_5,
  input  in_6,
  input  in_7,
  input  in_8,
  output _0b,
  output _0c,
  output _33,
  output _15,
  output _38,
  output _16,
  output _46,
  output _1f,
  output _29
);

  and u__0c (_0c, ~in_1, ~in_2, ~in_3, ~in_4, in_5, in_6, ~in_7, ~in_8);  // AND_Gate
  and u__15 (_15, ~in_1, ~in_2, ~in_3, in_4, ~in_5, in_6, ~in_7, in_8);  // AND_Gate
  and u__16 (_16, ~in_1, ~in_2, ~in_3, in_4, ~in_5, in_6, in_7, ~in_8);  // AND_Gate
  and u__1f (_1f, ~in_1, ~in_2, ~in_3, in_4, in_5, in_6, in_7, in_8);  // AND_Gate
  and u__29 (_29, ~in_1, ~in_2, in_3, ~in_4, ~in_5, in_6, in_7, ~in_8);  // AND_Gate
  and u__0b (_0b, ~in_1, ~in_2, ~in_3, ~in_4, in_5, ~in_6, in_7, in_8);  // AND_Gate
  and u__33 (_33, ~in_1, ~in_2, in_3, in_4, ~in_5, ~in_6, in_7, in_8);  // AND_Gate
  and u__38 (_38, ~in_1, ~in_2, in_3, in_4, in_5, ~in_6, ~in_7, ~in_8);  // AND_Gate
  and u__46 (_46, ~in_1, in_2, ~in_3, ~in_4, ~in_5, in_6, in_7, ~in_8);  // AND_Gate
endmodule
