// Logisim project main.circ as structural Verilog: 2 circuits, main circuit main
module main (
  input  in_1,
  input  in_2,
  input  in_3,
  input  in_4,
  input  in_5,
  input  in_6
);

  wire clock_1_out;
  wire [7:0] PC_q;
  wire [15:0] IR_q, ram_1_data;

  Clock clock_1 (.out(clock_1_out));
  Counter PC (.load(in_1), .count(in_2), .Q(PC_q), .clk(clock_1_out), .clr(in_6));  // open: D, carry
  RAM #(.dataWidth(16), .bus("separate")) ram_1 (
    .addr(PC_q), .data(ram_1_data), .str(in_3), .clk(clock_1_out), .ld(in_4), .clr(in_5));  // open: din, sel
  Register ACC ();  // open: D, en, Q, clk, clr
  Register #(.width(16)) IR (.D(ram_1_data), .Q(IR_q), .clk(clock_1_out));  // open: en, clr
endmodule

module Comparador (
  input  in_1,
  input  in_2,
  input  in_3,
  input  in_4,
  input  in_5,
  input  in_6,
  input  in_7,
  input  in_8,
  input  in_9,
  input  in_10,
  input  in_11,
  input  in_12,
  input  in_13,
  input  in_14,
  input  in_15,
  input  in_16
);
endmodule
